# Fritzing sketch Motor_DC (saved by Fritzing 0.9.2b)
breadboards: 1

parts:
  U1 = Vibration Motor- ROB-08449 [package=vibe-motor-10mm]
  Parte1 = Arduino Uno (Rev3) - ICSP
  Q1 = npn-Powertransistor [package="TO220 [THT]"]
  R1 = Resistor [tolerance=±5% resistance=220 package="1206 [SMD]"]

nets:
  N1: U1.+, Parte1.GND, Q1.emitter
  N2: U1.-, Q1.collector
  N3: Parte1.D9_PWM, R1.Pin_0
  N4: Q1.base, R1.Pin_1
